// Digital circuit CG-16-1-ALU.dig as structural Verilog
// Arithmetic and Logic Unit of this processor.
module CG_16_1_ALU (
  input  [15:0] A,
  input  [15:0] B,
  input  [4:0] OP,
  input  C_in,
  output C_out,
  output Z,
  output N,
  output [15:0] X,
  output A_gt_B,
  output A_eq_B,
  output A_lt_B,
  output [15:0] X_high
);

  wire add_1_c_o, comparator_2_gt, Decrement_c_o, Increment_c_o, sub_1_c_o;
  wire [4:0] bitcount_1_out;
  wire [15:0] add_1_s, and_1_out, ASL_out, ASR_out, Decrement_s, Increment_s, LSL_out, LSR_out, or_1_out,
       ROL_out, ROR_out, Signed_Division_q, Signed_Division_r, sub_1_s, Unsigned_Division_q,
       Unsigned_Division_r, xor_1_out;
  wire [31:0] Signed_Multiply_mul, Unsigned_Multiply_mul;

  Add #(.Bits(16)) add_1 (.a(A), .b(B), .c_i(C_in), .s(add_1_s), .c_o(add_1_c_o));
  Sub #(.Bits(16)) sub_1 (.a(A), .b(B), .c_i(C_in), .s(sub_1_s), .c_o(sub_1_c_o));
  Add #(.Bits(16)) Increment (.a(A), .b({16{1'b0}}), .c_i(1'b1), .s(Increment_s), .c_o(Increment_c_o));
  Sub #(.Bits(16)) Decrement (.a(A), .b({16{1'b0}}), .c_i(1'b1), .s(Decrement_s), .c_o(Decrement_c_o));
  Mul #(.Bits(16)) Unsigned_Multiply (.a(A), .b(B), .mul(Unsigned_Multiply_mul));
  Div #(.Bits(16)) Unsigned_Division (.a(A), .b(B), .q(Unsigned_Division_q), .r(Unsigned_Division_r));
  Mul #(.Signed("true"), .Bits(16)) Signed_Multiply (.a(A), .b(B), .mul(Signed_Multiply_mul));
  Div #(.Bits(16)) Signed_Division (.a(A), .b(B), .q(Signed_Division_q), .r(Signed_Division_r));
  assign and_1_out = A & B;  // And and_1, 16 bits wide
  assign or_1_out = A | B;  // Or or_1, 16 bits wide
  assign xor_1_out = A ^ B;  // XOr xor_1, 16 bits wide
  BarrelShifter #(.Bits(16)) LSL (.in(A), .shift(5'b00001), .out(LSL_out));
  BarrelShifter #(.Bits(16), .direction("right")) LSR (.in(A), .shift(5'b00001), .out(LSR_out));
  BarrelShifter #(.barrelShifterMode("rotate"), .Bits(16)) ROL (.in(A), .shift(5'b00001), .out(ROL_out));
  BarrelShifter #(.barrelShifterMode("rotate"), .Bits(16), .direction("right")) ROR (
    .in(A), .shift(5'b00001), .out(ROR_out));
  BarrelShifter #(.barrelShifterMode("rotate"), .Bits(16)) ASL (.in(A), .shift(5'b00001), .out(ASL_out));
  BarrelShifter #(.barrelShifterMode("rotate"), .Bits(16), .direction("right")) ASR (
    .in(A), .shift(5'b00001), .out(ASR_out));
  Comparator #(.Bits(16)) comparator_1 (.a(A), .b(B), .gt(A_gt_B), .eq(A_eq_B), .lt(A_lt_B));
  Multiplexer #(.Selector_Bits(5), .Bits(16)) multiplexer_1 (
    .sel(OP), .in_0({16{1'b0}}), .in_1({16{1'b0}}), .in_2({16{1'b0}}), .in_3({16{1'b0}}), .in_4({16{1'b0}}),
    .in_5(Unsigned_Multiply_mul[31:16]), .in_6(Unsigned_Division_r), .in_7(Signed_Multiply_mul[31:16]),
    .in_8(Signed_Division_r), .in_9({16{1'b0}}), .in_10({16{1'b0}}), .in_11({16{1'b0}}), .in_12({16{1'b0}}),
    .in_13({16{1'b0}}), .in_14({16{1'b0}}), .in_15({16{1'b0}}), .in_16({16{1'b0}}), .in_17({16{1'b0}}),
    .in_18({16{1'b0}}), .in_19({16{1'b0}}), .in_20({16{1'b0}}), .in_21({16{1'b0}}), .in_22({16{1'b0}}),
    .in_23({16{1'b0}}), .in_24({16{1'b0}}), .in_25({16{1'b0}}), .in_26({16{1'b0}}), .in_27({16{1'b0}}),
    .in_28({16{1'b0}}), .in_29({16{1'b0}}), .in_30({16{1'b0}}), .in_31({16{1'b0}}), .out(X_high));
  Multiplexer #(.Selector_Bits(5), .Bits(16)) multiplexer_2 (
    .sel(OP), .in_0(add_1_s), .in_1(sub_1_s), .in_2(Increment_s), .in_3(Decrement_s),
    .in_4(Unsigned_Multiply_mul[15:0]), .in_5(Unsigned_Division_q), .in_6(Signed_Multiply_mul[15:0]),
    .in_7(Signed_Division_q), .in_8(and_1_out), .in_9(or_1_out), .in_10(xor_1_out), .in_11(LSL_out),
    .in_12(LSR_out), .in_13(ROL_out), .in_14(ROR_out), .in_15(ASL_out), .in_16(ASR_out), .in_17({16{1'b0}}),
    .in_18({16{1'b0}}), .in_19({16{1'b0}}), .in_20({16{1'b0}}), .in_21({16{1'b0}}), .in_22({16{1'b0}}),
    .in_23({16{1'b0}}), .in_24({16{1'b0}}), .in_25({16{1'b0}}), .in_26({16{1'b0}}), .in_27({16{1'b0}}),
    .in_28({16{1'b0}}), .in_29({16{1'b0}}), .in_30({16{1'b0}}), .in_31({16{1'b0}}), .out({N, X[14:0]}));
  Comparator #(.Bits(16)) Zero_check (.a({N, X[14:0]}), .b({16{1'b0}}), .eq(Z));  // open: gt, lt
  BitCount #(.Bits(16)) bitcount_1 (.in(X_high), .out(bitcount_1_out));
  Comparator #(.Bits(5)) comparator_2 (.a(bitcount_1_out), .b({5{1'b0}}), .gt(comparator_2_gt));  // open: eq, lt
  Multiplexer #(.Selector_Bits(5)) multiplexer_3 (
    .sel(OP), .in_0(add_1_c_o), .in_1(sub_1_c_o), .in_2(Increment_c_o), .in_3(Decrement_c_o),
    .in_4(comparator_2_gt), .in_5(comparator_2_gt), .in_6(comparator_2_gt), .in_7(comparator_2_gt),
    .in_8(1'b0), .in_9(1'b0), .in_10(1'b0), .in_11(1'b0), .in_12(1'b0), .in_13(1'b0), .in_14(1'b0),
    .in_15(1'b0), .in_16(1'b0), .in_17(1'b0), .in_18(1'b0), .in_19(1'b0), .in_20(1'b0), .in_21(1'b0),
    .in_22(1'b0), .in_23(1'b0), .in_24(1'b0), .in_25(1'b0), .in_26(1'b0), .in_27(1'b0), .in_28(1'b0),
    .in_29(1'b0), .in_30(1'b0), .in_31(1'b0), .out(C_out));

  assign X[15] = N;

  // Notes on the sheet:
  //   A: Number A
  //   B: Number B
  //   C_out: Carry, Set to 1 if this operation is causing an overflow.
  //   Z: Set to 1 if the current output is zero
  //   N: Set to 1 if the current operation is resulting in a negative number.
  //   OP: Operation to perform
  //   C_in: Carry bit from last OP
  //   X: Output of operation
  //   X_high: Output of operation, high set of 2 bytes from Multiplication and Division
  //   Negative Check
endmodule
