// Digital circuit CG-16-1-Processor.dig as structural Verilog
module CG_16_1_Processor (
  input  clk,
  input  in_2,
  input  in_3,
  input  [7:0] in_4
);

  wire aawrite, aluread, aluselectxhigh, aluwriteflags, and_1_out, and_2_out, and_3_out, and_4_out,
       and_5_out, and_6_out, aread, awrite, bsread, bswrite, carry, carryclear, carryset, ccclr, clock,
       comparator_1_eq, comparator_2_eq, comparator_3_gt, condjumpddesired, demultiplexer_1_out_0,
       demultiplexer_1_out_1, demultiplexer_1_out_2, demultiplexer_1_out_3, demultiplexer_1_out_4,
       demultiplexer_1_out_5, demultiplexer_1_out_6, demultiplexer_1_out_7, demultiplexer_1_out_8,
       demultiplexer_1_out_9, demultiplexer_1_out_10, demultiplexer_1_out_11, demultiplexer_1_out_12,
       demultiplexer_1_out_13, demultiplexer_1_out_14, demultiplexer_1_out_15, demultiplexer_1_out_16,
       demultiplexer_1_out_17, demultiplexer_1_out_18, demultiplexer_1_out_19, demultiplexer_1_out_20,
       demultiplexer_1_out_21, demultiplexer_1_out_22, demultiplexer_1_out_23, demultiplexer_1_out_24,
       disableinterrupts, enableinterrupts, equalclear, equalset, Fetch_Check_lt, flagsread, flagswrite,
       Gr_RAM_check_eq, haltclock, irread, irwrite, lessthanclear, lessthanset, mmuread, mmuwrite,
       morethanclear, morethanset, multiplexer_6_out, negativeclear, negativeset, or_1_out, or_2_out,
       Page_Select_q, pageclear, pageset, pcbsclr, pcbsread, pcbswrite, pcclr, pcinc, pcread, pcwrite,
       Program_Counter_ovf, ROM_check_eq, sbread, sbwrite, stclr, stdec, stinc, stread, stwrite, telnet_1_av,
       telnet_1_out, xread, xwrite, yread, ywrite, zeroclear, zeroset, zread, zwrite;
  wire [2:0] condjump;
  wire [3:0] Control_Counter_out;
  wire [4:0] aluop;
  wire [6:1] flags;
  wire [7:0] address_bus, Program_Counter_Bank_Select_out;
  wire [11:0] aluflags;
  wire [11:1] busflags;
  wire [15:0] accumulator, address, blockramdualport_1_d, bus, cg_16_1_alu_1_x, cg_16_1_alu_1_x_high,
       instruction, multiplexer_1_out, Program_Counter_out, Stack_Base_Pointer_q, Stack_Top_Pointer_out, x,
       X_q, Y_q, Z_q;
  wire [63:0] Control_ROM_d, multiplexer_2_out;
  wire [63:11] multiplexer_3_out;

  Telnet #(.port(7000)) telnet_1 (.in(in_4), .C(clock), .wr(in_2), .rd(in_3), .out(telnet_1_out), .av(telnet_1_av));
  Multiplexer #(.Bits(16)) multiplexer_1 (.sel(aluread), .in_0(bus), .in_1(x), .out(multiplexer_1_out));
  or or_1 (or_1_out, stdec, stinc);
  assign clock = ~haltclock ? clk : 1'bz;  // DriverInvSel driverinvsel_1
  Register #(.Bits(16)) u_X (.D(bus), .C(clock), .en(xwrite), .Q(X_q));
  Register #(.Bits(16)) Y (.D(bus), .C(clock), .en(ywrite), .Q(Y_q));
  Register #(.Bits(16)) Z (.D(bus), .C(clock), .en(zwrite), .Q(Z_q));
  Register #(.Bits(16)) u_Accumulator (.D(multiplexer_1_out), .C(clock), .en(awrite), .Q(accumulator));
  CounterPreset #(.Bits(16)) Program_Counter (
    .en(pcinc), .C(clock), .dir(1'b0), .in(bus), .ld(pcwrite), .clr(pcclr), .out(Program_Counter_out),
    .ovf(Program_Counter_ovf));
  Register #(.Bits(16)) Instruction_Register (.D(bus), .C(clock), .en(irwrite), .Q(instruction));
  CounterPreset #(.Bits(16)) Stack_Top_Pointer (
    .en(or_1_out), .C(clock), .dir(stdec), .in(bus), .ld(stwrite), .clr(stclr), .out(Stack_Top_Pointer_out));  // open: ovf
  Register #(.Bits(16)) Stack_Base_Pointer (.D(bus), .C(clock), .en(sbwrite), .Q(Stack_Base_Pointer_q));
  Register #(.Bits(8)) Bank_Select_Register (.D(bus[7:0]), .C(clock), .en(bswrite), .Q(address_bus));
  Register #(.Bits(16)) Address_Access_Register (.D(bus), .C(clock), .en(aawrite), .Q(address));
  Register #(.Bits(16)) Interrupt_Register (.D(bus), .C(clock), .en(aawrite));  // open: Q
  assign bus = xread ? X_q : 16'bz;  // Driver driver_1
  assign bus = yread ? Y_q : 16'bz;  // Driver driver_2
  assign bus = zread ? Z_q : 16'bz;  // Driver driver_3
  assign bus = aread ? accumulator : 16'bz;  // Driver driver_4
  assign bus = pcread ? Program_Counter_out : 16'bz;  // Driver driver_5
  CounterPreset #(.Bits(8)) Program_Counter_Bank_Select (
    .en(Program_Counter_ovf), .C(clock), .dir(1'b0), .in(bus[7:0]), .ld(pcbswrite), .clr(pcbsclr),
    .out(Program_Counter_Bank_Select_out));  // open: ovf
  assign bus = irread ? instruction : 16'bz;  // Driver driver_6
  assign bus = stread ? Stack_Top_Pointer_out : 16'bz;  // Driver driver_7
  assign bus = sbread ? Stack_Base_Pointer_q : 16'bz;  // Driver driver_8
  assign bus = bsread ? {{8{1'b0}}, address_bus} : 16'bz;  // Driver driver_9
  assign bus = pcbsread ? {{8{1'b0}}, Program_Counter_Bank_Select_out} : 16'bz;  // Driver driver_10
  Counter #(.Bits(4)) Control_Counter (.en(~clock), .C(~clock), .clr(ccclr), .out(Control_Counter_out));  // open: ovf
  RS_FF Carry_Flag (.S(carryset), .C(clock), .R(carryclear), .Q(carry));  // open: nQ
  RS_FF Zero_Flag (.S(zeroset), .C(clock), .R(zeroclear), .Q(flags[1]));  // open: nQ
  RS_FF Negative_Flag (.S(negativeset), .C(clock), .R(negativeclear), .Q(flags[2]));  // open: nQ
  RS_FF More_Than_Flag (.S(morethanset), .C(clock), .R(morethanclear), .Q(flags[3]));  // open: nQ
  RS_FF Equal_Flag (.S(equalset), .C(clock), .R(equalclear), .Q(flags[4]));  // open: nQ
  RS_FF Less_Than_Flag (.S(lessthanset), .C(clock), .R(lessthanclear), .Q(flags[5]));  // open: nQ
  RS_FF Interrupt_Disable_Flag (.S(disableinterrupts), .C(clock), .R(enableinterrupts), .Q(flags[6]));  // open: nQ
  assign bus = flagsread ? {{9{1'b0}}, flags, carry} : 16'bz;  // Driver driver_11
  ROM #(.AddrBits(20), .Bits(64)) Control_ROM (.A({instruction, Control_Counter_out}), .sel(1'b1), .D(Control_ROM_d));
  LED u_Carry (.in(carry));
  LED Zero (.in(flags[1]));
  LED Negative (.in(flags[2]));
  LED More_Than (.in(flags[3]));
  LED Equal (.in(flags[4]));
  LED Less_Than (.in(flags[5]));
  LED Interrupt_Disable (.in(flags[6]));
  Multiplexer #(.Bits(64)) multiplexer_2 (
    .sel(Control_Counter_out[0]), .in_0(64'h2000400), .in_1(64'h40001), .out(multiplexer_2_out));
  Demultiplexer #(.Selector_Bits(8)) demultiplexer_1 (
    .sel(instruction[7:0]), .in(1'b1), .out_0(demultiplexer_1_out_0), .out_1(demultiplexer_1_out_1),
    .out_2(demultiplexer_1_out_2), .out_3(demultiplexer_1_out_3), .out_4(demultiplexer_1_out_4),
    .out_5(demultiplexer_1_out_5), .out_6(demultiplexer_1_out_6), .out_7(demultiplexer_1_out_7),
    .out_8(demultiplexer_1_out_8), .out_9(demultiplexer_1_out_9), .out_10(demultiplexer_1_out_10),
    .out_11(demultiplexer_1_out_11), .out_12(demultiplexer_1_out_12), .out_13(demultiplexer_1_out_13),
    .out_14(demultiplexer_1_out_14), .out_15(demultiplexer_1_out_15), .out_16(demultiplexer_1_out_16),
    .out_17(demultiplexer_1_out_17), .out_18(demultiplexer_1_out_18), .out_19(demultiplexer_1_out_19),
    .out_20(demultiplexer_1_out_20), .out_21(demultiplexer_1_out_21), .out_22(demultiplexer_1_out_22),
    .out_23(demultiplexer_1_out_23), .out_24(demultiplexer_1_out_24));  // open: out_25, out_26, out_27, out_28, out_29, out_30, out_31, out_32, out_33, out_34, out_35, out_36, out_37, out_38, out_39, out_40, out_41, out_42, out_43, out_44, out_45, out_46, out_47, out_48, out_49, out_50, out_51, out_52, out_53, out_54, out_55, out_56, out_57, out_58, out_59, out_60, out_61, out_62, out_63, out_64, out_65, out_66, out_67, out_68, out_69, out_70, out_71, out_72, out_73, out_74, out_75, out_76, out_77, out_78, out_79, out_80, out_81, out_82, out_83, out_84, out_85, out_86, out_87, out_88, out_89, out_90, out_91, out_92, out_93, out_94, out_95, out_96, out_97, out_98, out_99, out_100, out_101, out_102, out_103, out_104, out_105, out_106, out_107, out_108, out_109, out_110, out_111, out_112, out_113, out_114, out_115, out_116, out_117, out_118, out_119, out_120, out_121, out_122, out_123, out_124, out_125, out_126, out_127, out_128, out_129, out_130, out_131, out_132, out_133, out_134, out_135, out_136, out_137, out_138, out_139, out_140, out_141, out_142, out_143, out_144, out_145, out_146, out_147, out_148, out_149, out_150, out_151, out_152, out_153, out_154, out_155, out_156, out_157, out_158, out_159, out_160, out_161, out_162, out_163, out_164, out_165, out_166, out_167, out_168, out_169, out_170, out_171, out_172, out_173, out_174, out_175, out_176, out_177, out_178, out_179, out_180, out_181, out_182, out_183, out_184, out_185, out_186, out_187, out_188, out_189, out_190, out_191, out_192, out_193, out_194, out_195, out_196, out_197, out_198, out_199, out_200, out_201, out_202, out_203, out_204, out_205, out_206, out_207, out_208, out_209, out_210, out_211, out_212, out_213, out_214, out_215, out_216, out_217, out_218, out_219, out_220, out_221, out_222, out_223, out_224, out_225, out_226, out_227, out_228, out_229, out_230, out_231, out_232, out_233, out_234, out_235, out_236, out_237, out_238, out_239, out_240, out_241, out_242, out_243, out_244, out_245, out_246, out_247, out_248, out_249, out_250, out_251, out_252, out_253, out_254, out_255
  Comparator #(.Bits(4)) Fetch_Check (.a(Control_Counter_out), .b(4'b0010), .lt(Fetch_Check_lt));  // open: gt, eq
  Multiplexer #(.Bits(64)) multiplexer_3 (
    .sel(Fetch_Check_lt), .in_0(Control_ROM_d), .in_1(multiplexer_2_out),
    .out({multiplexer_3_out[63], pageclear, pageset, haltclock, condjumpddesired, condjump, aluselectxhigh, aluread, stclr, stdec, stinc, multiplexer_3_out[50:49], flagswrite, flagsread, ccclr, enableinterrupts, disableinterrupts, multiplexer_3_out[43:32], aluwriteflags, aluop, aawrite, bswrite, bsread, sbwrite, sbread, stwrite, stread, irwrite, irread, pcbsclr, pcbswrite, pcbsread, pcclr, pcinc, multiplexer_3_out[11], pcread, awrite, aread, zwrite, zread, ywrite, yread, xwrite, xread, mmuwrite, mmuread}));
  LED NOP (.in(demultiplexer_1_out_0));
  LED LDA (.in(demultiplexer_1_out_1));
  LED LDX (.in(demultiplexer_1_out_2));
  LED LDY (.in(demultiplexer_1_out_3));
  LED LDZ (.in(demultiplexer_1_out_4));
  LED LDS (.in(demultiplexer_1_out_5));
  LED STA (.in(demultiplexer_1_out_6));
  LED STX (.in(demultiplexer_1_out_7));
  LED STY (.in(demultiplexer_1_out_8));
  LED STZ (.in(demultiplexer_1_out_9));
  LED TAX (.in(demultiplexer_1_out_10));
  LED TAY (.in(demultiplexer_1_out_11));
  LED TAZ (.in(demultiplexer_1_out_12));
  LED TXA (.in(demultiplexer_1_out_13));
  LED TYA (.in(demultiplexer_1_out_14));
  LED TZA (.in(demultiplexer_1_out_15));
  LED TBA (.in(demultiplexer_1_out_16));
  LED TTX (.in(demultiplexer_1_out_17));
  LED TXT (.in(demultiplexer_1_out_18));
  LED TTB (.in(demultiplexer_1_out_19));
  LED TBT (.in(demultiplexer_1_out_20));
  LED PHA (.in(demultiplexer_1_out_21));
  LED PHP (.in(demultiplexer_1_out_22));
  LED PLA (.in(demultiplexer_1_out_23));
  LED PLP (.in(demultiplexer_1_out_24));
  CG_16_1_ALU cg_16_1_alu_1 (
    .OP(aluop), .A(accumulator), .B(bus), .C_in(carry), .C_out(aluflags[0]), .Z(aluflags[2]),
    .N(aluflags[4]), .A_gt_B(aluflags[6]), .A_eq_B(aluflags[8]), .A_lt_B(aluflags[10]), .X(cg_16_1_alu_1_x),
    .X_high(cg_16_1_alu_1_x_high));
  Comparator #(.Bits(8)) Gr_RAM_check (.a(address_bus), .b({8{1'b1}}), .eq(Gr_RAM_check_eq));  // open: gt, lt
  Comparator #(.Bits(8)) ROM_check (.a(address_bus), .b({8{1'b0}}), .eq(ROM_check_eq));  // open: gt, lt
  and and_1 (and_1_out, Gr_RAM_check_eq, mmuread);
  Comparator #(.Bits(3)) comparator_1 (.a(condjump), .b(3'b000), .eq(comparator_1_eq));  // open: gt, lt
  assign pcwrite = comparator_1_eq ? multiplexer_3_out[11] : 1'bz;  // Driver driver_12
  Multiplexer #(.Bits(16)) multiplexer_4 (
    .sel(aluselectxhigh), .in_0(cg_16_1_alu_1_x), .in_1(cg_16_1_alu_1_x_high), .out(x));
  Multiplexer #(.Selector_Bits(2), .Bits(12)) multiplexer_5 (
    .sel({flagswrite, aluwriteflags}), .in_0(multiplexer_3_out[43:32]), .in_1(aluflags),
    .in_2({busflags[11], bus[5], busflags[9], bus[4], busflags[7], bus[3], busflags[5], bus[2], busflags[3], bus[1], busflags[1], bus[0]}),
    .in_3({12{1'b1}}),
    .out({lessthanclear, lessthanset, equalclear, equalset, morethanclear, morethanset, negativeclear, negativeset, zeroclear, zeroset, carryclear, carryset}));
  or or_2 (or_2_out, Gr_RAM_check_eq, ROM_check_eq);
  and and_2 (and_2_out, ROM_check_eq, mmuwrite);
  and and_3 (and_3_out, ROM_check_eq, mmuread);
  and and_4 (and_4_out, ~Gr_RAM_check_eq, mmuwrite);  // And
  and and_5 (and_5_out, mmuwrite, Gr_RAM_check_eq);
  RS_FF Page_Select (.S(pageset), .C(clock), .R(pageclear), .Q(Page_Select_q));  // open: nQ
  Stop Write_to_ROM_error (.stop(and_2_out));
  ROM #(.AddrBits(16), .isProgramMemory("true"), .Bits(16)) rom_1 (.A(address), .sel(and_3_out), .D(bus));
  BlockRAMDualPort #(.AddrBits(24), .Bits(16)) blockramdualport_1 (
    .A({address_bus, address}), .Din(bus), .str(and_4_out), .C(clock), .D(blockramdualport_1_d));
  GraphicCard #(.graphicHeight(160), .graphicWidth(200), .Bits(16)) graphiccard_1 (
    .A(address), .str(and_5_out), .C(clock), .ld(and_1_out), .B(Page_Select_q), .D(bus));
  not not_1 (aluflags[1], aluflags[0]);
  not not_2 (aluflags[3], aluflags[2]);
  not not_3 (aluflags[5], aluflags[4]);
  not not_4 (aluflags[7], aluflags[6]);
  not not_5 (aluflags[9], aluflags[8]);
  not not_6 (aluflags[11], aluflags[10]);
  assign bus = multiplexer_3_out[49] ? {{8{1'b0}}, instruction[7:0]} : 16'bz;  // Driver driver_13
  assign bus = multiplexer_3_out[50] ? {{8{1'b0}}, instruction[15:8]} : 16'bz;  // Driver driver_14
  and and_6 (and_6_out, mmuread, ~or_2_out);  // And
  assign bus = and_6_out ? blockramdualport_1_d : 16'bz;  // Driver driver_15
  Multiplexer #(.Selector_Bits(3)) multiplexer_6 (
    .sel(condjump), .in_0(1'b0), .in_1(carry), .in_2(flags[1]), .in_3(flags[2]), .in_4(flags[3]),
    .in_5(flags[4]), .in_6(flags[5]), .in_7(flags[6]), .out(multiplexer_6_out));
  Comparator comparator_2 (.a(multiplexer_6_out), .b(condjumpddesired), .eq(comparator_2_eq));  // open: gt, lt
  Comparator #(.Bits(3)) comparator_3 (.a(condjump), .b(3'b000), .gt(comparator_3_gt));  // open: eq, lt
  assign pcwrite = comparator_3_gt ? comparator_2_eq : 1'bz;  // Driver driver_16
  not not_7 (busflags[1], bus[0]);
  not not_8 (busflags[3], bus[1]);
  not not_9 (busflags[5], bus[2]);
  not not_10 (busflags[7], bus[3]);
  not not_11 (busflags[9], bus[4]);
  not not_12 (busflags[11], bus[5]);

  // Other names for the same wires on the sheet: busflags (some bits) = bus[5:0]; flags[0] = carry

  // Notes on the sheet:
  //   clk: Hz: 500
  //   Registers
  //   Flags
  //   Control Logic
  //   Fetch
  //   contents of Control_ROM (hex, n*v repeats v):
  //   0,0,400000000000
  //   MMU
  //   ALU
  //   microinstructions
  //   contents of rom_1 (hex, n*v repeats v):
  //   0,1,3,76d3,29*0,1
  //   Conditional Jumps
  //   Bus Flag Decoding
endmodule
